// Logisim project brojac.circ as structural Verilog: 2 circuits, main circuit main
module main (
  input  in_1
);

  wire clock_1_out, j_k_ff_1_q, j_k_ff_2_q, multiplexer_1_out, multiplexer_2_out, multiplexer_3_out,
       multiplexer_4_out, not_1_out, not_2_out, not_3_out, not_4_out;
  wire [1:0] kodiranje_1_b2;
  wire [2:0] counter_1_q;

  Clock clock_1 (.out(clock_1_out));
  Counter #(.width(3), .max('h4)) counter_1 (
    .Q(counter_1_q), .clk(clock_1_out), .clr(in_1));  // open: load, D, count, carry
  kodiranje kodiranje_1 (
    .a(counter_1_q[2]), .b(counter_1_q[1]), .c(counter_1_q[0]), .a2(kodiranje_1_b2[1]), .b2(kodiranje_1_b2[0]));
  J_K_Flip_Flop j_k_ff_1 (
    .J(multiplexer_3_out), .clk(clock_1_out), .K(multiplexer_4_out), .Q(j_k_ff_1_q));  // open: Qn, preset, en, reset
  not not_1 (not_1_out, j_k_ff_1_q);
  Multiplexer #(.select(2)) multiplexer_1 (
    .in0(1'b1), .in2(not_1_out), .out(multiplexer_1_out), .sel(kodiranje_1_b2));  // open: in1, in3, en
  not not_2 (not_2_out, j_k_ff_1_q);
  Multiplexer #(.select(2)) multiplexer_2 (
    .in0(not_2_out), .in2(not_3_out), .out(multiplexer_2_out), .sel(kodiranje_1_b2));  // open: in1, in3, en
  not not_3 (not_3_out, j_k_ff_1_q);
  Multiplexer #(.select(2)) multiplexer_3 (
    .in0(j_k_ff_2_q), .out(multiplexer_3_out), .sel(kodiranje_1_b2));  // open: in1, in2, in3, en
  not not_4 (not_4_out, j_k_ff_2_q);
  Multiplexer #(.select(2)) multiplexer_4 (
    .in0(not_4_out), .out(multiplexer_4_out), .sel(kodiranje_1_b2));  // open: in1, in2, in3, en
  J_K_Flip_Flop j_k_ff_2 (
    .J(multiplexer_1_out), .clk(clock_1_out), .K(multiplexer_2_out), .Q(j_k_ff_2_q));  // open: Qn, preset, en, reset
endmodule

module kodiranje (
  input  a,
  input  b,
  input  c,
  output a2,
  output b2
);

  wire not_1_out, not_2_out, not_3_out;

  not not_1 (not_1_out, b);
  not not_2 (not_2_out, c);
  not not_3 (not_3_out, a);
  and and_1 (a2, a, not_1_out, not_2_out);
  and and_2 (b2, not_3_out, b, c);
endmodule
